# Fritzing sketch Sketch breadboard (saved by Fritzing 0.9.9b)
circuit board: 14.6464cm x 11.3968cm
breadboards: 1

parts:
  M1 = Kaith switch socket
  M3 = Kaith switch socket
  M4 = Kaith switch socket
  M5 = Kaith switch socket
  M6 = Kaith switch socket
  M7 = Kaith switch socket
  M8 = Kaith switch socket
  M9 = Kaith switch socket
  M10 = Kaith switch socket
  M11 = Kaith switch socket
  M12 = Kaith switch socket
  M13 = Kaith switch socket
  M14 = Kaith switch socket
  M15 = Kaith switch socket
  M16 = Kaith switch socket
  M17 = Kaith switch socket
  M18 = Kaith switch socket
  M19 = Kaith switch socket
  D1 = Diode [package=diode-1n4148]
  Pro_Micro1 = Mone v3 SparkFun Pro Micro
  D2 = Diode [package=diode-1n4148]
  D3 = Diode [package=diode-1n4148]
  D4 = Diode [package=diode-1n4148]
  D5 = Diode [package=diode-1n4148]
  D6 = Diode [package=diode-1n4148]
  D7 = Diode [package=diode-1n4148]
  D8 = Diode [package=diode-1n4148]
  D9 = Diode [package=diode-1n4148]
  D10 = Diode [package=diode-1n4148]
  D11 = Diode [package=diode-1n4148]
  D12 = Diode [package=diode-1n4148]
  D13 = Diode [package=diode-1n4148]
  D14 = Diode [package=diode-1n4148]
  D15 = Diode [package=diode-1n4148]
  D16 = Diode [package=diode-1n4148]
  D17 = Diode [package=diode-1n4148]
  D18 = Diode [package=diode-1n4148]
  D19 = Diode [package=diode-1n4148]
  D20 = Diode [package=diode-1n4148]
  R2 = Mone v3 Rotary Potentiometer (Small) [package=THT]
  M2 = Kaith switch socket

nets:
  N1: M1.pin1, M5.pin1, M9.pin1, M13.pin1, Pro_Micro1.3
  N2: M1.pin2, D1.A
  N3: M3.pin1, M7.pin1, M11.pin1, M15.pin1, M16.pin1, Pro_Micro1.5
  N4: M3.pin2, D2.C, D4.A
  N5: M4.pin1, M8.pin1, M12.pin1, M19.pin1, Pro_Micro1.6
  N6: M4.pin2, D3.A, D4.C
  N7: M5.pin2, D5.A
  N8: M6.pin1, M10.pin1, M14.pin1, M17.pin1, Pro_Micro1.4, M2.pin1
  N9: M6.pin2, D5.C, D6.A
  N10: M7.pin2, D6.C, D8.A
  N11: M8.pin2, D7.A, D8.C
  N12: M9.pin2, D9.A
  N13: M10.pin2, D9.C, D12.A
  N14: M11.pin2, D11.A, D12.C
  N15: M12.pin2, D10.A, D11.C
  N16: M13.pin2, D13.A
  N17: M14.pin2, D17.A
  N18: M15.pin2, D16.A, D17.C
  N19: M16.pin2, D19.A
  N20: M17.pin2, D13.C, D20.A
  N21: M18.pin1, Pro_Micro1.7
  N22: M18.pin2, D18.A, D19.C, D20.C
  N23: M19.pin2, D15.A, D16.C
  N24: D1.C, D2.A, M2.pin2
  N25: Pro_Micro1.10, D18.C
  N26: Pro_Micro1.16, D14.C
  N27: Pro_Micro1.14, D10.C
  N28: Pro_Micro1.15, D7.C
  N29: Pro_Micro1.A0, D3.C
  N30: D14.A, D15.C, R2.SwitchGND

custom parts:
  Kaith switch socket: Kaith switch socket for MX series key switches.
  Mone v3 SparkFun Pro Micro: The Pro Micro is similar to the Pro Mini except with an ATmega32U4 on board. The USB transceiver inside the 32U4 allows us to add USB connectivity on-board and do away with bulky external USB interface. Based on: https://github.com/unorthodox-engineers/unorthodox-arduino/blob/master/Unorthodox/fritzing/parts/Pro%20Micro.fzpz
  Mone v3 Rotary Potentiometer (Small): A rotary adjustable resistor (potentiometer).
